# Fritzing sketch breadboard (saved by Fritzing 0.9.0b)
breadboards: 1

parts:
  Part1 = Spark Core (v1.0)
  R1 = Resistor [tolerance=±5% resistance=330 package="1206 [SMD]"]
  S1 = Reed switch [package=THT]

nets:
  N1: Part1.GND, R1.Pin_0
  N2: Part1.VIN, S1.pin_2
  N3: Part1.D0, R1.Pin_1, S1.pin_1
